// Digital circuit 03引用自定义组件.dig as structural Verilog
module \_03引用自定义组件  (
  input  in_2,
  output out_1
);

  // _02逻辑门 _02逻辑门_1: pin names not known; wires that end beside it: in_2, out_1
endmodule
