// Digital circuit 04与门.dig as structural Verilog
module \_04与门  (
  input  A1,
  input  A2,
  output B
);

  wire relay_1_p5;

  // Relay relay_1: pin names not known; wires that end beside it: A1, 1'b0, A2, 1'b1, relay_1_p5, relay_1_p5
  // Relay relay_2: pin names not known; wires that end beside it: 1'b0, B
endmodule
