// Digital circuit 05异或门.dig as structural Verilog
module \_05异或门  (
  input  A1,
  input  A2,
  output B
);

  wire and_1_out, and_2_out, not_1_out, not_2_out;

  not not_1 (not_1_out, A1);
  not not_2 (not_2_out, A2);
  and and_1 (and_1_out, not_1_out, A2);
  and and_2 (and_2_out, A1, not_2_out);
  or or_1 (B, and_1_out, and_2_out);
endmodule
