// Digital circuit 01全加器.dig as structural Verilog
module \_01全加器  (
  input  A_i,
  input  B_i,
  input  C_i_1,
  output S_i,
  output C_i
);

  wire \_01半加_2_p3 , \_01半加_2_p4 , \_01半加_2_p7 ;

  \_01半加  \_01半加_1  ();  // open: A, B, S, C
  // _01半加 _01半加_2: pin names not known; wires that end beside it: A_i, B_i, \_01半加_2_p3 , \_01半加_2_p4 , \_01半加_2_p4 , C_i_1, \_01半加_2_p7 , C_i, \_01半加_2_p7 , S_i
  // Or or_1 has open pins: In_1=\_01半加_2_p3 , In_2=open, out=open

  // Notes on the sheet:
  //   A_i: 加数A的第i位
  //   B_i: 加数B的第i位
  //   C_i_1: 来自低位的进位
  //   S_i: 求和结果第i位
  //   C_i: 向高位的进位
endmodule
