// Digital circuit 02加法.dig as structural Verilog
module \_02加法  (
  input  Cin,
  input  A,
  input  B,
  output S,
  output Cout
);

  wire \_01半加_1_c , \_01半加_1_s , \_01半加_2_c ;

  \_01半加  \_01半加_1  (.A(A), .B(B), .S(\_01半加_1_s ), .C(\_01半加_1_c ));
  \_01半加  \_01半加_2  (.A(Cin), .B(\_01半加_1_s ), .S(S), .C(\_01半加_2_c ));
  or or_1 (Cout, \_01半加_2_c , \_01半加_1_c );
endmodule
