// Digital circuit 02_EN开关SR寄存器.dig as structural Verilog
module \_02_EN开关SR寄存器  (
  input  S,
  input  en,
  input  R,
  output out_4,
  output out_5
);

  wire nand_1_out, nand_2_out;

  nand nand_1 (nand_1_out, S, en);
  nand nand_2 (nand_2_out, en, R);
  \_01_SR锁存器  \_01_sr锁存器_1  (.S(nand_1_out), .R(nand_2_out), .Q(out_4), .Q_2(out_5));

  // Notes on the sheet:
  //   en: 这是一个寄存器的使能开关
  //   使能开关
endmodule
