// Digital circuit 03_EN开关D寄存器.dig as structural Verilog
module \_03_EN开关D寄存器  (
  input  D,
  input  en,
  output Q,
  output Q_2
);

  wire nand_1_out, nand_2_out, not_1_out;

  not not_1 (not_1_out, D);
  nand nand_1 (nand_1_out, D, en);
  nand nand_2 (nand_2_out, en, not_1_out);
  \_01_SR锁存器  \_01_sr锁存器_1  (.S(nand_1_out), .R(nand_2_out), .Q(Q), .Q_2(Q_2));

  // Notes on the sheet:
  //   en: 这是一个寄存器的使能开关
  //   使能开关
endmodule
