// Digital circuit 04_D触发器.dig as structural Verilog
module \_04_D触发器  (
  input  D,
  input  en,
  output Q,
  output Q_2,
  output out_5
);

  wire not_1_out;

  not not_1 (not_1_out, en);
  \_03_EN开关D寄存器  \_03_en开关d寄存器_1  (.D(D), .en(not_1_out), .Q(out_5));  // open: Q_2
  \_03_EN开关D寄存器  \_03_en开关d寄存器_2  (.D(out_5), .en(en), .Q(Q), .Q_2(Q_2));

  // Notes on the sheet:
  //   en = 1时, 才会将D的数据记录到Q
  //   过程值
endmodule
