// Digital circuit 05_寄存器.dig as structural Verilog
module \_05_寄存器  (
  input  C,
  input  en,
  input  [3:0] D,
  output [3:0] Q
);

  wire and_1_out;

  and and_1 (and_1_out, C, en);
  Register register_1 (.D(D[0]), .C(and_1_out), .Q(Q[0]));  // open: en
  // Pins of 1 and 4 bits meet at D
  // Pins of 1 and 4 bits meet at Q
endmodule
