// Digital circuit 01_带记录的加法.dig as structural Verilog
module \_01_带记录的加法  (
  input  [15:0] B,
  input  in_2,
  input  clk,
  output [15:0] out_3
);

  wire [15:0] add_1_s;

  Add #(.Bits(16)) add_1 (.a(out_3), .b(B), .c_i(1'b0), .s(add_1_s));  // open: c_o
  Register #(.Bits(16)) register_1 (.D(add_1_s), .C(clk), .en(in_2), .Q(out_3));

  // Notes on the sheet:
  //   clk: Hz: 50
  //   a+b=s
  //   保存的数字作为下一次的值
endmodule
