// Digital circuit 1位复用器.dig as structural Verilog
module \_1位复用器  (
  input  S_2,
  input  S_1,
  input  sel,
  output S
);

  // RelayDT relaydt_1: pin names not known; wires that end beside it: sel, S_2, S_1, 1'b0, S

  // Notes on the sheet:
  //   复用器 / 选择器
endmodule
