// Digital circuit 2位复用器.dig as structural Verilog
module \_2位复用器  (
  input  S1,
  input  S2,
  input  S3,
  input  S4,
  input  [1:0] sel,
  output S
);

  wire \_1位复用器_1_s , \_1位复用器_2_s ;

  \_1位复用器  \_1位复用器_1  (.S_2(S1), .S_1(S2), .sel(sel[0]), .S(\_1位复用器_1_s ));
  \_1位复用器  \_1位复用器_2  (.S_2(S3), .S_1(S4), .sel(sel[0]), .S(\_1位复用器_2_s ));
  \_1位复用器  \_1位复用器_3  (.S_2(\_1位复用器_1_s ), .S_1(\_1位复用器_2_s ), .sel(sel[1]), .S(S));

  // Other names for the same wires on the sheet: SEL_0 = sel[0]; SEL_1 = sel[1]

  // Notes on the sheet:
  //   复用器 / 选择器
endmodule
