// Digital circuit 38译码器.dig as structural Verilog
module \_38译码器  (
  input  [2:0] A,
  output s_0,
  output s_1,
  output s_2,
  output s_3,
  output s_4,
  output s_5,
  output s_6,
  output s_7
);

  wire not_1_out, not_2_out, not_3_out;

  not not_1 (not_1_out, A[2]);
  not not_2 (not_2_out, A[1]);
  not not_3 (not_3_out, A[0]);
  and and_1 (s_0, not_3_out, not_2_out, not_1_out);
  and and_2 (s_1, A[0], not_2_out, not_1_out);
  and and_3 (s_2, not_3_out, A[1], not_1_out);
  and and_4 (s_3, A[0], A[1], not_1_out);
  and and_5 (s_4, not_3_out, not_2_out, A[2]);
  and and_6 (s_5, A[0], not_2_out, A[2]);
  and and_7 (s_6, not_3_out, A[1], A[2]);
  and and_8 (s_7, A[0], A[1], A[2]);

  // Other names for the same wires on the sheet: A_0 = A[0]; A_1 = A[1]; A_2 = A[2]
endmodule
