// Digital circuit 内存.dig as structural Verilog
module \内存  (
  input  [2:0] Addr,
  input  [15:0] D_in,
  input  C,
  input  str,
  input  ld,
  output [15:0] D_out,
  output [15:0] out_5,
  output [15:0] out_6,
  output [15:0] out_7,
  output [15:0] out_8,
  output [15:0] out_9,
  output [15:0] out_10,
  output [15:0] out_11,
  output [15:0] out_12
);

  wire clock, s_0, s_1, s_2, s_3, s_4, s_5, s_6, s_7;
  wire [15:0] multiplexer_1_out;

  and and_1 (clock, C, str);
  \_38译码器  \_38译码器_1  (
    .A(Addr), .s_0(s_0), .s_1(s_1), .s_2(s_2), .s_3(s_3), .s_4(s_4), .s_5(s_5), .s_6(s_6), .s_7(s_7));
  Register #(.Bits(16)) register_1 (.D(D_in), .C(clock), .en(s_0), .Q(out_5));
  Register #(.Bits(16)) register_2 (.D(D_in), .C(clock), .en(s_2), .Q(out_6));
  Register #(.Bits(16)) register_3 (.D(D_in), .C(clock), .en(s_4), .Q(out_12));
  Register #(.Bits(16)) register_4 (.D(D_in), .C(clock), .en(s_6), .Q(out_11));
  Register #(.Bits(16)) register_5 (.D(D_in), .C(clock), .en(s_1), .Q(out_7));
  Register #(.Bits(16)) register_6 (.D(D_in), .C(clock), .en(s_3), .Q(out_8));
  Register #(.Bits(16)) register_7 (.D(D_in), .C(clock), .en(s_5), .Q(out_9));
  Register #(.Bits(16)) register_8 (.D(D_in), .C(clock), .en(s_7), .Q(out_10));
  Multiplexer #(.Bits(16), .Selector_Bits(3)) multiplexer_1 (
    .sel(Addr), .in_0(out_5), .in_1(out_7), .in_2(out_6), .in_3(out_8), .in_4(out_12), .in_5(out_9),
    .in_6(out_11), .in_7(out_10), .out(multiplexer_1_out));
  assign D_out = ld ? multiplexer_1_out : 16'bz;  // Driver driver_1

  // Other names for the same wires on the sheet: Q_0[15:0] = out_5; Q_1[15:0] = out_7; Q_2[15:0] = out_6;
  //   Q_3[15:0] = out_8; Q_4[15:0] = out_12; Q_5[15:0] = out_9; Q_6[15:0] = out_11; Q_7[15:0] = out_10

  // Notes on the sheet:
  //   Addr: 地址
  //   D_in: 输入
  //   str: 写入开关
  //   ld: 输出开关
  //   定义一个开关
  //   输出开关
endmodule
