// Digital circuit 计数器_跳转.dig as structural Verilog
module \计数器_跳转  (
  input  en_pc,
  input  C,
  input  [3:0] addr,
  input  ld_pc,
  output [3:0] D_out,
  output ovf
);

  wire or_1_out;
  wire [3:0] add_1_s, multiplexer_1_out;

  Multiplexer #(.Bits(4)) multiplexer_1 (.sel(ld_pc), .in_0(add_1_s), .in_1(addr), .out(multiplexer_1_out));
  or or_1 (or_1_out, ld_pc, en_pc);
  Register #(.Bits(4)) register_1 (.D(multiplexer_1_out), .C(C), .en(or_1_out), .Q(D_out));
  Add #(.Bits(4)) add_1 (.a(D_out), .b(4'b0001), .c_i(1'b0), .s(add_1_s), .c_o(ovf));

  // Notes on the sheet:
  //   表示溢出
endmodule
