// Digital circuit 计算单元_跳转.dig as structural Verilog
module \计算单元_跳转  (
  input  clk,
  output [15:0] out_2,
  output [1:0] out_3,
  output [15:0] out_4,
  output [3:0] out_5
);

  wire C, en_a, en_pc, halt, ld, ld_pc, str;
  wire [1:0] sel_a, sel_b;
  wire [14:7] \指令集_d ;
  wire [15:0] alu_1_s, register_1_q, \数据集_d ;

  and and_1 (C, clk, halt);
  \计数器_跳转  \u_计数器_跳转_1  (.en_pc(en_pc), .C(C), .addr(out_4[3:0]), .ld_pc(ld_pc), .D_out(out_5));  // open: ovf
  EEPROMDualPort #(.AddrBits(4), .Bits(16)) \u_指令集  (
    .A(out_5), .Din({16{1'b0}}), .str(1'b0), .C(C), .ld(1'b1),
    .D({halt, \指令集_d [14:13], ld, str, ld_pc, \指令集_d [9], en_pc, \指令集_d [7], en_a, sel_b, sel_a, out_3}));
  Register #(.Bits(16)) register_1 (.D(alu_1_s), .C(C), .en(en_a), .Q(register_1_q));
  EEPROMDualPort #(.AddrBits(4), .Bits(16)) \u_数据集  (.A(out_5), .Din(out_2), .str(str), .C(C), .ld(ld), .D(\数据集_d ));
  Multiplexer #(.Selector_Bits(2), .Bits(16)) multiplexer_1 (
    .sel(sel_a), .in_0(register_1_q), .in_1({16{1'b0}}), .in_2({16{1'b0}}), .in_3({16{1'b0}}), .out(out_2));
  Multiplexer #(.Selector_Bits(2), .Bits(16)) multiplexer_2 (
    .sel(sel_b), .in_0(\数据集_d ), .in_1({16{1'b0}}), .in_2({16{1'b0}}), .in_3({16{1'b0}}), .out(out_4));
  ALU alu_1 (.A(out_2), .B(out_4), .sel(out_3), .S(alu_1_s));  // open: C_out, DF

  // Other names for the same wires on the sheet: address[3:0] = out_5; D_in[15:0] = out_2

  // Notes on the sheet:
  //   控制条件
  //   contents of 指令集 (hex, n*v repeats v):
  //   9144,a140,9141,9140,8950,9144,9140,9141,9150,9504
  //   contents of 数据集 (hex, n*v repeats v):
  //   1,2,3,4,3,a,b,1,5,2
  //   寄存器
  //   计算单元
endmodule
