// Digital circuit 02_2位比较器.dig as structural Verilog
module \_02_2位比较器  (
  input  [1:0] in_1,
  input  [1:0] in_2,
  output out_3,
  output out_4
);

  \_02_1位比较器  \_02_1位比较器_1  (.A(in_1[0]), .B(in_2[0]), .ZF(out_3));
  \_02_1位比较器  \_02_1位比较器_2  (.A(in_1[1]), .B(in_2[1]), .ZF(out_4));
  // Pins of 1 and 2 bits meet at in_1
  // Pins of 1 and 2 bits meet at in_2
endmodule
