// Digital circuit opcode_指令.dig as structural Verilog
module \opcode_指令  (
  input  [4:0] opcode,
  input  [4:0] cmp,
  input  clock,
  output [1:0] alu,
  output [1:0] sel_a,
  output [1:0] sel_b,
  output en_a,
  output en_pc,
  output je_en,
  output jump_en,
  output str,
  output ld,
  output halt,
  output en_addr
);

  wire d_ff_1_nq, d_ff_1_q;
  wire [14:7] lookuptable_1_out;

  D_FF d_ff_1 (.D(d_ff_1_nq), .C(clock), .Q(d_ff_1_q), .nQ(d_ff_1_nq));
  LookUpTable #(.Bits(16)) lookuptable_1 (
    .in0(opcode[0]), .in1(opcode[1]), .in2(opcode[2]), .in3(opcode[3]), .in4(opcode[4]), .in5(cmp[0]),
    .in6(d_ff_1_q),
    .out({halt, lookuptable_1_out[14], en_addr, ld, str, jump_en, je_en, en_pc, lookuptable_1_out[7], en_a, sel_b, sel_a, alu}));
  // Pins of 1 and 2 bits meet at alu
  // Pins of 1 and 2 bits meet at sel_a
  // Pins of 1 and 2 bits meet at sel_b
  // Pins of 1 and 5 bits meet at cmp

  // Notes on the sheet:
  //   contents of lookuptable_1 (hex, n*v repeats v):
  //   9*b100,23*0,b100,32*0,9144,9140,9041,9042,9043,9810,8400,8000
  //   ,24*0,9144,9140,9041,9042,9043,9810,8400,8000
endmodule
