// Digital circuit 带储存的计算单元.dig as structural Verilog
module \带储存的计算单元  (
  input  in_1,
  input  [1:0] sel,
  input  [15:0] d_in,
  input  clk,
  input  Str,
  input  Id,
  output [15:0] A,
  output [2:0] out_8
);

  wire C, comparator_1_lt;
  wire [15:0] alu_1_s, eepromdualport_1_d;

  Comparator #(.Bits(3)) comparator_1 (.a(out_8), .b(3'b100), .lt(comparator_1_lt));  // open: gt, eq
  and and_1 (C, clk, comparator_1_lt);
  // 计数器 计数器_1: pin names not known; wires that end beside it: in_1, C, out_8
  Register #(.Bits(16)) register_1 (.D(alu_1_s), .C(C), .en(in_1), .Q(A));
  EEPROMDualPort #(.AddrBits(3), .Bits(16)) eepromdualport_1 (
    .A(out_8), .Din(d_in), .str(Str), .C(C), .ld(Id), .D(eepromdualport_1_d));
  ALU alu_1 (.A(A), .B(eepromdualport_1_d), .sel(sel), .S(alu_1_s));  // open: C_out, DF

  // Other names for the same wires on the sheet: D_out[2:0] = out_8

  // Notes on the sheet:
  //   使能开关
  //   控制条件
  //   寄存器
  //   contents of eepromdualport_1 (hex, n*v repeats v):
  //   1,2,3,4,5,6,7,8
  //   计算单元
endmodule
