// Digital circuit 计数器_11位.dig as structural Verilog
module \计数器_11位  (
  input  en_pc,
  input  C,
  input  [10:0] addr,
  input  ld_pc,
  output [10:0] D_out,
  output ovf
);

  wire or_1_out;
  wire [10:0] add_1_s, multiplexer_1_out;

  Multiplexer #(.Bits(11)) multiplexer_1 (.sel(ld_pc), .in_0(add_1_s), .in_1(addr), .out(multiplexer_1_out));
  or or_1 (or_1_out, ld_pc, en_pc);
  Register #(.Bits(11)) register_1 (.D(multiplexer_1_out), .C(C), .en(or_1_out), .Q(D_out));
  Add #(.Bits(11)) add_1 (.a(D_out), .b(11'h1), .c_i(1'b0), .s(add_1_s), .c_o(ovf));

  // Notes on the sheet:
  //   表示溢出
endmodule
