// Digital circuit 计算单元.dig as structural Verilog
module \计算单元  (
  input  in_1,
  input  clk,
  output [3:0] out_3,
  output [15:0] out_4,
  output [1:0] out_5,
  output [15:0] out_6
);

  wire C, halt, ld, str;
  wire [1:0] sel_a, sel_b;
  wire [14:6] \指令集_d ;
  wire [15:0] alu_1_s, register_1_q, \数据集_d ;

  and and_1 (C, clk, halt);
  \计数器  \u_计数器_1  (.en(in_1), .C(C), .D_out(out_3));  // open: ovf
  Register #(.Bits(16)) register_1 (.D(alu_1_s), .C(C), .en(in_1), .Q(register_1_q));
  EEPROMDualPort #(.AddrBits(4), .Bits(16)) \u_数据集  (.A(out_3), .Din(out_4), .str(str), .C(C), .ld(ld), .D(\数据集_d ));
  EEPROMDualPort #(.AddrBits(4), .Bits(16)) \u_指令集  (
    .A(out_3), .Din({16{1'b0}}), .str(1'b0), .C(C), .ld(1'b1),
    .D({halt, \指令集_d [14:13], ld, str, \指令集_d [10:6], sel_b, sel_a, out_5}));
  Multiplexer #(.Selector_Bits(2), .Bits(16)) multiplexer_1 (
    .sel(sel_a), .in_0(register_1_q), .in_1({16{1'b0}}), .in_2({16{1'b0}}), .in_3({16{1'b0}}), .out(out_4));
  Multiplexer #(.Selector_Bits(2), .Bits(16)) multiplexer_2 (
    .sel(sel_b), .in_0(\数据集_d ), .in_1({16{1'b0}}), .in_2({16{1'b0}}), .in_3({16{1'b0}}), .out(out_6));
  ALU alu_1 (.A(out_4), .B(out_6), .sel(out_5), .S(alu_1_s));  // open: C_out, DF

  // Other names for the same wires on the sheet: address[3:0] = out_3; D_in[15:0] = out_4

  // Notes on the sheet:
  //   使能开关
  //   控制条件
  //   contents of 数据集 (hex, n*v repeats v):
  //   1,2,3,4,0,a,b,1
  //   contents of 指令集 (hex, n*v repeats v):
  //   9004,9000,9001,9000,8810,9004,9000,9001,8810
  //   寄存器
  //   计算单元
endmodule
