// Digital circuit 计算单元_指令.dig as structural Verilog
module \计算单元_指令  (
  input  clk,
  output [15:0] out_2,
  output [1:0] out_3
);

  wire and_1_out, C, en_a, en_addr, en_pc, halt, je_en, jump_en, ld, or_1_out, str, ZF, \比较寄存器_q ;
  wire [1:0] sel_a, sel_b;
  wire [4:0] opcode;
  wire [10:0] multiplexer_1_out, \指令寄存器_q , \计数器_11位_1_d_out ;
  wire [15:0] alu_1_s, D_out, register_1_q, \内存_d ;

  Register \u_比较寄存器  (.D(ZF), .C(C), .en(en_a), .Q(\比较寄存器_q ));
  Register #(.Bits(16)) \u_指令寄存器  (.D(D_out), .C(C), .en(en_addr), .Q({opcode, \指令寄存器_q }));
  and and_1 (and_1_out, je_en, \比较寄存器_q );
  or or_1 (or_1_out, jump_en, and_1_out);
  \计数器_11位  \u_计数器_11位_1  (
    .en_pc(en_pc), .C(C), .addr(\指令寄存器_q ), .ld_pc(or_1_out), .D_out(\计数器_11位_1_d_out ));  // open: ovf
  Multiplexer #(.Bits(11)) multiplexer_1 (
    .sel(en_pc), .in_0(\指令寄存器_q ), .in_1(\计数器_11位_1_d_out ), .out(multiplexer_1_out));
  and and_2 (C, clk, halt);
  // opcode_指令 opcode_指令_1: pin names not known; wires that end beside it: opcode, \比较寄存器_q , C, out_3, sel_a, sel_b, en_a, en_pc, je_en, jump_en, str, ld, halt, en_addr
  Register #(.Bits(16)) register_1 (.D(alu_1_s), .C(C), .en(en_a), .Q(register_1_q));
  EEPROMDualPort #(.AddrBits(11), .Bits(16)) \u_内存  (
    .A(multiplexer_1_out), .Din(out_2), .str(str), .C(C), .ld(ld), .D(\内存_d ));
  Multiplexer #(.Selector_Bits(2), .Bits(16)) multiplexer_2 (
    .sel(sel_a), .in_0(register_1_q), .in_1({16{1'b0}}), .in_2({16{1'b0}}), .in_3({16{1'b0}}), .out(out_2));
  Multiplexer #(.Selector_Bits(2), .Bits(16)) multiplexer_3 (
    .sel(sel_b), .in_0(\内存_d ), .in_1({16{1'b0}}), .in_2({16{1'b0}}), .in_3({16{1'b0}}), .out(D_out));
  ALU alu_1 (.A(out_2), .B(D_out), .sel(out_3), .S(alu_1_s), .DF(ZF));  // open: C_out

  // Other names for the same wires on the sheet: D_in[15:0] = out_2

  // Notes on the sheet:
  //   控制条件
  //   contents of 内存 (hex, n*v repeats v):
  //   ,a140,9141,9140,8950,9144,9140,9141,9150,9504
  //   寄存器
  //   计算单元
endmodule
