// Digital circuit 02非门.dig as structural Verilog
module \_02非门  (
  input  A,
  output B
);

  // Relay relay_1: pin names not known; wires that end beside it: A, 1'b1, 1'b0, B
  PullDown pulldown_1 (.out(B));
endmodule
