// Digital circuit 03加发器.dig as structural Verilog
// 8位全加器 - 由8个全加器级联组成
module \_03加发器  (
  input  [3:0] A,
  input  [3:0] B,
  output [3:0] S,
  output Cout
);

  wire \_02加法_1_cout , \_02加法_2_cout , \_02加法_3_cout ;

  \_02加法  \_02加法_1  (.Cin(1'b0), .A(A[0]), .B(B[0]), .S(S[0]), .Cout(\_02加法_1_cout ));
  \_02加法  \_02加法_2  (.Cin(\_02加法_3_cout ), .A(A[2]), .B(B[2]), .S(S[2]), .Cout(\_02加法_2_cout ));
  \_02加法  \_02加法_3  (.Cin(\_02加法_1_cout ), .A(A[1]), .B(B[1]), .S(S[1]), .Cout(\_02加法_3_cout ));
  \_02加法  \_02加法_4  (.Cin(\_02加法_2_cout ), .A(A[3]), .B(B[3]), .S(S[3]), .Cout(Cout));
endmodule
