// Digital circuit 05减法.dig as structural Verilog
module \_05减法  (
  input  A,
  input  B,
  input  C_in,
  output S,
  output C_out
);

  wire \_04半减_1_c , \_04半减_1_s , \_04半减_2_c ;

  \_04半减  \_04半减_1  (.A(A), .B(B), .S(\_04半减_1_s ), .C(\_04半减_1_c ));
  \_04半减  \_04半减_2  (.A(\_04半减_1_s ), .B(C_in), .S(S), .C(\_04半减_2_c ));
  or or_1 (C_out, \_04半减_2_c , \_04半减_1_c );

  // Notes on the sheet:
  //   C_in: 借位
endmodule
