// Digital circuit 06减法器.dig as structural Verilog
// 8位全加器 - 由8个全加器级联组成
module \_06减法器  (
  input  [3:0] A,
  input  [3:0] B,
  input  C_in,
  output [3:0] S,
  output C_out
);

  wire \_05减法_1_c_out , \_05减法_2_c_out , \_05减法_3_c_out ;

  \_05减法  \_05减法_1  (.A(A[0]), .B(B[0]), .C_in(C_in), .S(S[0]), .C_out(\_05减法_1_c_out ));
  \_05减法  \_05减法_2  (.A(A[2]), .B(B[2]), .C_in(\_05减法_3_c_out ), .S(S[2]), .C_out(\_05减法_2_c_out ));
  \_05减法  \_05减法_3  (.A(A[1]), .B(B[1]), .C_in(\_05减法_1_c_out ), .S(S[1]), .C_out(\_05减法_3_c_out ));
  \_05减法  \_05减法_4  (.A(A[3]), .B(B[3]), .C_in(\_05减法_2_c_out ), .S(S[3]), .C_out(C_out));
endmodule
